// Logisim project project.circ as structural Verilog: 5 circuits, main circuit main
module main (
  input  in_1,
  input  in_2,
  input  in_3,
  input  in_4,
  input  in_5,
  input  in_6,
  input  in_7,
  input  in_8,
  input  in_9,
  input  in_10,
  input  in_11,
  output SIGNED_OVERLOAD,
  output ZERO,
  output NEGATIVE,
  output OVERFLOW
);

  wire a6_1_out_15, a6_1_out_16, a6_1_out_17, a6_1_out_18, A6_LEFT_DOOR, A6_RIGHT_DOOR, ADD, and_1_out,
       and_2_out, and_3_out, and_4_out, and_5_out, and_6_out, and_7_out, and_8_out, and_9_out, and_10_out,
       and_11_out, and_12_out, and_13_out, and_14_out, and_15_out, and_16_out, and_17_out, and_18_out,
       and_19_out, and_20_out, and_21_out, and_22_out, and_23_out, and_24_out, and_25_out, and_26_out,
       and_27_out, and_28_out, and_29_out, and_30_out, and_31_out, and_32_out, and_33_out, and_34_out,
       and_35_out, and_36_out, and_37_out, and_38_out, and_39_out, and_40_out, and_41_out, and_42_out,
       and_43_out, and_44_out, and_45_out, and_46_out, and_47_out, and_48_out, and_49_out, and_50_out,
       and_51_out, and_52_out, and_53_out, and_54_out, and_55_out, and_56_out, and_57_out, and_58_out,
       and_59_out, and_60_out, and_61_out, and_62_out, and_63_out, and_64_out, and_65_out, and_66_out,
       and_67_out, and_68_out, and_69_out, and_70_out, and_71_out, and_72_out, and_73_out, and_74_out,
       and_75_out, and_76_out, and_77_out, and_78_out, and_79_out, and_80_out, and_81_out, and_82_out,
       and_83_out, and_84_out, and_85_out, and_86_out, and_87_out, and_88_out, and_89_out, and_90_out,
       and_91_out, and_92_out, and_93_out, and_94_out, and_95_out, and_96_out, and_97_out, and_98_out,
       and_99_out, and_100_out, and_101_out, and_102_out, and_103_out, and_104_out, and_105_out, and_106_out,
       and_107_out, and_108_out, and_109_out, and_110_out, and_111_out, and_112_out, and_113_out,
       and_114_out, and_115_out, and_116_out, and_117_out, and_118_out, and_119_out, and_120_out,
       and_121_out, and_122_out, and_123_out, and_124_out, and_125_out, and_126_out, and_127_out,
       and_128_out, and_129_out, and_130_out, and_131_out, and_132_out, and_133_out, and_134_out,
       and_135_out, and_136_out, and_137_out, and_138_out, and_141_out, and_142_out, and_143_out,
       and_144_out, and_146_out, and_151_out, and_152_out, and_153_out, and_154_out, and_155_out, Clk,
       COMPUTE, d_ff_1_q, d_ff_2_q, d_ff_3_q, d_ff_4_q, d_ff_5_q, d_ff_6_q, d_ff_7_q, d_ff_8_q, d_ff_9_q,
       d_ff_10_q, d_ff_11_q, d_ff_12_q, d_ff_13_q, d_ff_14_q, d_ff_15_q, d_ff_16_q, d_ff_17_q, d_ff_18_q,
       d_ff_19_q, d_ff_20_q, d_ff_21_q, d_ff_22_q, d_ff_23_q, d_ff_24_q, d_ff_25_q, d_ff_26_q, d_ff_27_q,
       d_ff_28_q, d_ff_29_q, d_ff_30_q, d_ff_31_q, d_ff_32_q, d_ff_33_q, d_ff_34_q, d_ff_35_q, d_ff_36_q,
       d_ff_37_q, d_ff_38_q, d_ff_39_q, d_ff_40_q, d_ff_41_q, d_ff_42_q, d_ff_43_q, d_ff_44_q, d_ff_45_q,
       d_ff_46_q, d_ff_47_q, d_ff_48_q, d_ff_49_q, d_ff_50_q, d_ff_51_q, d_ff_52_q, d_ff_53_q, d_ff_54_q,
       d_ff_55_q, d_ff_56_q, d_ff_57_q, d_ff_58_q, d_ff_59_q, d_ff_60_q, d_ff_61_q, d_ff_62_q, d_ff_63_q,
       d_ff_64_q, d_ff_65_q, d_ff_66_q, d_ff_67_q, d_ff_68_q, d_ff_69_q, d_ff_70_q, d_ff_71_q, d_ff_72_q,
       d_ff_73_q, d_ff_74_q, d_ff_75_q, d_ff_76_q, d_ff_77_q, d_ff_78_q, d_ff_79_q, d_ff_80_q, d_ff_81_q,
       d_ff_87_q, d_ff_88_q, d_ff_90_q, d_ff_91_q, d_ff_92_q, d_ff_93_q, d_ff_96_q, d_ff_97_q, d_ff_98_q,
       displayhelper_1_bit1_0, displayhelper_1_bit1_1, displayhelper_1_bot0, displayhelper_1_botleft0,
       displayhelper_1_botright0, displayhelper_1_mid0, displayhelper_1_top0, displayhelper_1_topleft0,
       displayhelper_1_topright0, gotoCU, gotoIR, HALT, LOAD, MINI_INSTRUCTION_COMPUTE, MINI_INSTRUCTION_END,
       MINI_INSTRUCTION_START, not_1_out, not_2_out, not_3_out, not_4_out, not_5_out, not_6_out, not_7_out,
       not_8_out, not_9_out, not_10_out, not_11_out, not_12_out, not_13_out, not_14_out, not_15_out,
       not_16_out, not_17_out, not_18_out, not_19_out, not_21_out, not_22_out, not_23_out, not_24_out,
       or_1_out, or_2_out, or_3_out, or_4_out, or_5_out, or_6_out, or_7_out, or_8_out, or_9_out, or_10_out,
       or_11_out, or_12_out, or_13_out, or_14_out, or_15_out, or_16_out, or_17_out, or_18_out, or_19_out,
       or_20_out, or_21_out, or_22_out, or_23_out, or_24_out, or_25_out, or_26_out, or_27_out, or_28_out,
       or_29_out, or_30_out, or_31_out, or_32_out, or_33_out, or_34_out, or_35_out, or_36_out, or_38_out,
       or_39_out, or_40_out, or_41_out, or_42_out, or_43_out, or_45_out, or_46_out, or_47_out, pc_1_haltout,
       pc_1_outbit0, pc_1_outbit1, pc_1_outbit2, R0_Read_Write_out, R1_Read_Write_out, RAM_DOOR,
       RAM_DOOR_MINI, RAM_MINI_INSTRUCTION, REGIST, REGIST_SAVE, REGISTER_DOOR, SAVE, SUB, WRITE_RESULT,
       xor_1_out;

  Clock clock_1 (.out(Clk));
  D_Flip_Flop #(.trigger("falling")) d_ff_1 (.D(or_45_out), .clk(Clk), .Q(d_ff_1_q));  // open: Qn, preset, reset
  D_Flip_Flop #(.trigger("falling")) d_ff_2 (.D(or_46_out), .clk(Clk), .Q(d_ff_2_q));  // open: Qn, preset, reset
  and and_1 (and_1_out, d_ff_1_q, d_ff_2_q, Clk, d_ff_3_q);
  and and_2 (and_2_out, d_ff_1_q, d_ff_2_q, Clk, not_1_out);
  not not_1 (not_1_out, d_ff_3_q);
  not not_2 (not_2_out, d_ff_2_q);
  and and_3 (and_3_out, d_ff_1_q, not_2_out, Clk, d_ff_3_q);
  not not_3 (not_3_out, d_ff_2_q);
  and and_4 (and_4_out, d_ff_1_q, not_3_out, Clk, not_4_out);
  not not_4 (not_4_out, d_ff_3_q);
  not not_5 (not_5_out, d_ff_1_q);
  and and_5 (and_5_out, not_5_out, d_ff_2_q, Clk, d_ff_3_q);
  not not_6 (not_6_out, d_ff_1_q);
  and and_6 (and_6_out, not_6_out, d_ff_2_q, Clk, not_7_out);
  not not_7 (not_7_out, d_ff_3_q);
  not not_8 (not_8_out, d_ff_1_q);
  not not_9 (not_9_out, d_ff_2_q);
  and and_7 (and_7_out, not_8_out, not_9_out, Clk, d_ff_3_q);
  not not_10 (not_10_out, d_ff_1_q);
  not not_11 (not_11_out, d_ff_2_q);
  and and_8 (and_8_out, not_10_out, not_11_out, Clk, not_12_out);
  not not_12 (not_12_out, d_ff_3_q);
  D_Flip_Flop #(.trigger("falling")) d_ff_3 (.D(or_47_out), .clk(Clk), .Q(d_ff_3_q));  // open: Qn, preset, reset
  and and_9 (and_9_out, and_1_out, not_13_out);
  and and_10 (and_10_out, and_2_out, not_13_out);
  and and_11 (and_11_out, and_3_out, not_13_out);
  and and_12 (and_12_out, and_4_out, not_13_out);
  and and_13 (and_13_out, and_5_out, not_13_out);
  and and_14 (and_14_out, and_6_out, not_13_out);
  and and_15 (and_15_out, and_7_out, not_13_out);
  and and_16 (and_16_out, and_8_out, not_13_out);
  not not_13 (not_13_out, d_ff_4_q);
  D_Flip_Flop #(.trigger("falling")) d_ff_4 (.D(xor_1_out), .clk(Clk), .Q(d_ff_4_q));  // open: Qn, preset, reset
  xor xor_1 (xor_1_out, REGIST_SAVE, or_1_out);
  not not_14 (not_14_out, and_17_out);
  and and_17 (and_17_out, or_38_out, Clk);
  and and_18 (and_18_out, and_1_out, not_13_out, d_ff_13_q);
  and and_19 (and_19_out, and_2_out, not_13_out, d_ff_13_q);
  and and_20 (and_20_out, and_3_out, not_13_out, d_ff_13_q);
  and and_21 (and_21_out, and_4_out, not_13_out, d_ff_13_q);
  and and_22 (and_22_out, and_5_out, not_13_out, d_ff_13_q);
  and and_23 (and_23_out, and_6_out, not_13_out, d_ff_13_q);
  and and_24 (and_24_out, and_7_out, not_13_out, d_ff_13_q);
  and and_25 (and_25_out, and_8_out, not_13_out, d_ff_13_q);
  or or_1 (or_1_out, not_14_out, LOAD);
  Clock clock_2 (.out(Clk));
  D_Flip_Flop #(.trigger("high")) d_ff_5 (.D(and_18_out), .clk(and_9_out), .Q(d_ff_5_q));  // open: Qn, preset, reset
  D_Flip_Flop #(.trigger("high")) d_ff_6 (.D(and_19_out), .clk(and_10_out), .Q(d_ff_6_q));  // open: Qn, preset, reset
  D_Flip_Flop #(.trigger("high")) d_ff_7 (.D(and_20_out), .clk(and_11_out), .Q(d_ff_7_q));  // open: Qn, preset, reset
  D_Flip_Flop #(.trigger("high")) d_ff_8 (.D(and_21_out), .clk(and_12_out), .Q(d_ff_8_q));  // open: Qn, preset, reset
  D_Flip_Flop #(.trigger("high")) d_ff_9 (.D(and_22_out), .clk(and_13_out), .Q(d_ff_9_q));  // open: Qn, preset, reset
  D_Flip_Flop #(.trigger("high")) d_ff_10 (.D(and_23_out), .clk(and_14_out), .Q(d_ff_10_q));  // open: Qn, preset, reset
  D_Flip_Flop #(.trigger("high")) d_ff_11 (.D(and_24_out), .clk(and_15_out), .Q(d_ff_11_q));  // open: Qn, preset, reset
  D_Flip_Flop #(.trigger("high")) d_ff_12 (.D(and_25_out), .clk(and_16_out), .Q(d_ff_12_q));  // open: Qn, preset, reset
  and and_26 (and_26_out, or_11_out, SAVE);
  and and_27 (and_27_out, or_10_out, or_3_out);
  or or_2 (or_2_out, and_28_out, and_29_out, and_30_out, and_31_out, and_32_out, and_33_out, and_34_out, and_35_out);
  and and_28 (and_28_out, d_ff_5_q, and_1_out, d_ff_4_q);
  and and_29 (and_29_out, d_ff_6_q, and_2_out, d_ff_4_q);
  and and_30 (and_30_out, d_ff_7_q, and_3_out, d_ff_4_q);
  and and_31 (and_31_out, d_ff_8_q, and_4_out, d_ff_4_q);
  and and_32 (and_32_out, d_ff_9_q, and_5_out, d_ff_4_q);
  and and_33 (and_33_out, d_ff_10_q, and_6_out, d_ff_4_q);
  and and_34 (and_34_out, d_ff_11_q, and_7_out, d_ff_4_q);
  and and_35 (and_35_out, d_ff_12_q, and_8_out, d_ff_4_q);
  D_Flip_Flop #(.trigger("falling")) d_ff_13 (.D(and_26_out), .clk(Clk), .Q(d_ff_13_q));  // open: Qn, preset, reset
  and and_36 (and_36_out, or_10_out, SAVE);
  and and_37 (and_37_out, or_11_out, or_3_out);
  and and_38 (and_38_out, or_9_out, or_3_out);
  and and_39 (and_39_out, or_8_out, or_3_out);
  or or_3 (or_3_out, RAM_DOOR, RAM_DOOR_MINI);
  D_Flip_Flop #(.trigger("falling")) d_ff_14 (.D(and_36_out), .clk(Clk), .Q(d_ff_14_q));  // open: Qn, preset, reset
  and and_40 (and_40_out, or_9_out, SAVE);
  D_Flip_Flop #(.trigger("high")) d_ff_15 (.D(or_2_out), .clk(Clk), .Q(d_ff_15_q));  // open: Qn, preset, reset
  and and_41 (and_41_out, and_1_out, not_13_out, d_ff_14_q);
  D_Flip_Flop #(.trigger("high")) d_ff_16 (.D(and_41_out), .clk(and_9_out), .Q(d_ff_16_q));  // open: Qn, preset, reset
  and and_42 (and_42_out, and_2_out, not_13_out, d_ff_14_q);
  D_Flip_Flop #(.trigger("high")) d_ff_17 (.D(and_42_out), .clk(and_10_out), .Q(d_ff_17_q));  // open: Qn, preset, reset
  and and_43 (and_43_out, and_3_out, not_13_out, d_ff_14_q);
  D_Flip_Flop #(.trigger("high")) d_ff_18 (.D(and_43_out), .clk(and_11_out), .Q(d_ff_18_q));  // open: Qn, preset, reset
  and and_44 (and_44_out, and_4_out, not_13_out, d_ff_14_q);
  D_Flip_Flop #(.trigger("high")) d_ff_19 (.D(and_44_out), .clk(and_12_out), .Q(d_ff_19_q));  // open: Qn, preset, reset
  and and_45 (and_45_out, and_5_out, not_13_out, d_ff_14_q);
  D_Flip_Flop #(.trigger("high")) d_ff_20 (.D(and_45_out), .clk(and_13_out), .Q(d_ff_20_q));  // open: Qn, preset, reset
  and and_46 (and_46_out, and_6_out, not_13_out, d_ff_14_q);
  D_Flip_Flop #(.trigger("high")) d_ff_21 (.D(and_46_out), .clk(and_14_out), .Q(d_ff_21_q));  // open: Qn, preset, reset
  and and_47 (and_47_out, and_7_out, not_13_out, d_ff_14_q);
  D_Flip_Flop #(.trigger("high")) d_ff_22 (.D(and_47_out), .clk(and_15_out), .Q(d_ff_22_q));  // open: Qn, preset, reset
  and and_48 (and_48_out, and_8_out, not_13_out, d_ff_14_q);
  D_Flip_Flop #(.trigger("high")) d_ff_23 (.D(and_48_out), .clk(and_16_out), .Q(d_ff_23_q));  // open: Qn, preset, reset
  D_Flip_Flop #(.trigger("falling")) d_ff_24 (.D(and_40_out), .clk(Clk), .Q(d_ff_24_q));  // open: Qn, preset, reset
  and and_49 (and_49_out, or_8_out, SAVE);
  D_Flip_Flop #(.trigger("high")) d_ff_25 (.D(or_4_out), .clk(Clk), .Q(d_ff_25_q));  // open: Qn, preset, reset
  or or_4 (or_4_out, and_50_out, and_51_out, and_52_out, and_53_out, and_54_out, and_55_out, and_56_out, and_57_out);
  and and_50 (and_50_out, d_ff_16_q, and_1_out, d_ff_4_q);
  and and_51 (and_51_out, d_ff_17_q, and_2_out, d_ff_4_q);
  and and_52 (and_52_out, d_ff_18_q, and_3_out, d_ff_4_q);
  and and_53 (and_53_out, d_ff_19_q, and_4_out, d_ff_4_q);
  and and_54 (and_54_out, d_ff_20_q, and_5_out, d_ff_4_q);
  and and_55 (and_55_out, d_ff_21_q, and_6_out, d_ff_4_q);
  and and_56 (and_56_out, d_ff_22_q, and_7_out, d_ff_4_q);
  and and_57 (and_57_out, d_ff_23_q, and_8_out, d_ff_4_q);
  D_Flip_Flop #(.trigger("falling")) d_ff_26 (.D(and_49_out), .clk(Clk), .Q(d_ff_26_q));  // open: Qn, preset, reset
  D_Flip_Flop #(.trigger("high")) d_ff_27 (.D(or_5_out), .clk(Clk), .Q(d_ff_27_q));  // open: Qn, preset, reset
  D_Flip_Flop d_ff_28 (.D(and_37_out), .clk(Clk), .Q(d_ff_28_q));  // open: Qn, preset, reset
  D_Flip_Flop d_ff_29 (.D(and_27_out), .clk(Clk), .Q(d_ff_29_q));  // open: Qn, preset, reset
  D_Flip_Flop d_ff_30 (.D(and_38_out), .clk(Clk), .Q(d_ff_30_q));  // open: Qn, preset, reset
  D_Flip_Flop d_ff_31 (.D(and_39_out), .clk(Clk), .Q(d_ff_31_q));  // open: Qn, preset, reset
  D_Flip_Flop #(.trigger("high")) d_ff_32 (.D(or_6_out), .clk(Clk), .Q(d_ff_32_q));  // open: Qn, preset, reset
  and and_58 (and_58_out, and_1_out, not_13_out, d_ff_24_q);
  D_Flip_Flop #(.trigger("high")) d_ff_33 (.D(and_58_out), .clk(and_9_out), .Q(d_ff_33_q));  // open: Qn, preset, reset
  and and_59 (and_59_out, and_2_out, not_13_out, d_ff_24_q);
  D_Flip_Flop #(.trigger("high")) d_ff_34 (.D(and_59_out), .clk(and_10_out), .Q(d_ff_34_q));  // open: Qn, preset, reset
  and and_60 (and_60_out, and_3_out, not_13_out, d_ff_24_q);
  D_Flip_Flop #(.trigger("high")) d_ff_35 (.D(and_60_out), .clk(and_11_out), .Q(d_ff_35_q));  // open: Qn, preset, reset
  and and_61 (and_61_out, and_4_out, not_13_out, d_ff_24_q);
  D_Flip_Flop #(.trigger("high")) d_ff_36 (.D(and_61_out), .clk(and_12_out), .Q(d_ff_36_q));  // open: Qn, preset, reset
  and and_62 (and_62_out, and_5_out, not_13_out, d_ff_24_q);
  D_Flip_Flop #(.trigger("high")) d_ff_37 (.D(and_62_out), .clk(and_13_out), .Q(d_ff_37_q));  // open: Qn, preset, reset
  and and_63 (and_63_out, and_6_out, not_13_out, d_ff_24_q);
  D_Flip_Flop #(.trigger("high")) d_ff_38 (.D(and_63_out), .clk(and_14_out), .Q(d_ff_38_q));  // open: Qn, preset, reset
  and and_64 (and_64_out, and_7_out, not_13_out, d_ff_24_q);
  D_Flip_Flop #(.trigger("high")) d_ff_39 (.D(and_64_out), .clk(and_15_out), .Q(d_ff_39_q));  // open: Qn, preset, reset
  and and_65 (and_65_out, and_8_out, not_13_out, d_ff_24_q);
  D_Flip_Flop #(.trigger("high")) d_ff_40 (.D(and_65_out), .clk(and_16_out), .Q(d_ff_40_q));  // open: Qn, preset, reset
  or or_5 (or_5_out, and_66_out, and_67_out, and_68_out, and_69_out, and_70_out, and_71_out, and_72_out, and_73_out);
  and and_66 (and_66_out, d_ff_33_q, and_1_out, d_ff_4_q);
  and and_67 (and_67_out, d_ff_34_q, and_2_out, d_ff_4_q);
  and and_68 (and_68_out, d_ff_35_q, and_3_out, d_ff_4_q);
  and and_69 (and_69_out, d_ff_36_q, and_4_out, d_ff_4_q);
  and and_70 (and_70_out, d_ff_37_q, and_5_out, d_ff_4_q);
  and and_71 (and_71_out, d_ff_38_q, and_6_out, d_ff_4_q);
  and and_72 (and_72_out, d_ff_39_q, and_7_out, d_ff_4_q);
  and and_73 (and_73_out, d_ff_40_q, and_8_out, d_ff_4_q);
  Clock clock_3 (.out(Clk));
  and and_74 (and_74_out, d_ff_15_q, or_7_out);
  and and_75 (and_75_out, d_ff_25_q, or_7_out);
  and and_76 (and_76_out, d_ff_27_q, or_7_out);
  and and_77 (and_77_out, and_1_out, not_13_out, d_ff_26_q);
  D_Flip_Flop #(.trigger("high")) d_ff_41 (.D(and_77_out), .clk(and_9_out), .Q(d_ff_41_q));  // open: Qn, preset, reset
  and and_78 (and_78_out, and_2_out, not_13_out, d_ff_26_q);
  D_Flip_Flop #(.trigger("high")) d_ff_42 (.D(and_78_out), .clk(and_10_out), .Q(d_ff_42_q));  // open: Qn, preset, reset
  and and_79 (and_79_out, and_3_out, not_13_out, d_ff_26_q);
  D_Flip_Flop #(.trigger("high")) d_ff_43 (.D(and_79_out), .clk(and_11_out), .Q(d_ff_43_q));  // open: Qn, preset, reset
  and and_80 (and_80_out, and_4_out, not_13_out, d_ff_26_q);
  D_Flip_Flop #(.trigger("high")) d_ff_44 (.D(and_80_out), .clk(and_12_out), .Q(d_ff_44_q));  // open: Qn, preset, reset
  and and_81 (and_81_out, and_5_out, not_13_out, d_ff_26_q);
  D_Flip_Flop #(.trigger("high")) d_ff_45 (.D(and_81_out), .clk(and_13_out), .Q(d_ff_45_q));  // open: Qn, preset, reset
  and and_82 (and_82_out, and_6_out, not_13_out, d_ff_26_q);
  D_Flip_Flop #(.trigger("high")) d_ff_46 (.D(and_82_out), .clk(and_14_out), .Q(d_ff_46_q));  // open: Qn, preset, reset
  and and_83 (and_83_out, and_7_out, not_13_out, d_ff_26_q);
  D_Flip_Flop #(.trigger("high")) d_ff_47 (.D(and_83_out), .clk(and_15_out), .Q(d_ff_47_q));  // open: Qn, preset, reset
  and and_84 (and_84_out, and_8_out, not_13_out, d_ff_26_q);
  D_Flip_Flop #(.trigger("high")) d_ff_48 (.D(and_84_out), .clk(and_16_out), .Q(d_ff_48_q));  // open: Qn, preset, reset
  and and_85 (and_85_out, d_ff_32_q, or_7_out);
  or or_6 (or_6_out, and_86_out, and_87_out, and_88_out, and_89_out, and_90_out, and_91_out, and_92_out, and_93_out);
  and and_86 (and_86_out, d_ff_41_q, and_1_out, d_ff_4_q);
  and and_87 (and_87_out, d_ff_42_q, and_2_out, d_ff_4_q);
  and and_88 (and_88_out, d_ff_43_q, and_3_out, d_ff_4_q);
  and and_89 (and_89_out, d_ff_44_q, and_4_out, d_ff_4_q);
  and and_90 (and_90_out, d_ff_45_q, and_5_out, d_ff_4_q);
  and and_91 (and_91_out, d_ff_46_q, and_6_out, d_ff_4_q);
  and and_92 (and_92_out, d_ff_47_q, and_7_out, d_ff_4_q);
  and and_93 (and_93_out, d_ff_48_q, and_8_out, d_ff_4_q);
  D_Flip_Flop d_ff_49 (.D(d_ff_12_q), .clk(Clk), .Q(d_ff_49_q));  // open: Qn, preset, reset
  D_Flip_Flop d_ff_50 (.D(d_ff_23_q), .clk(Clk), .Q(d_ff_50_q));  // open: Qn, preset, reset
  D_Flip_Flop d_ff_51 (.D(d_ff_40_q), .clk(Clk), .Q(d_ff_51_q));  // open: Qn, preset, reset
  D_Flip_Flop d_ff_52 (.D(d_ff_48_q), .clk(Clk), .Q(d_ff_52_q));  // open: Qn, preset, reset
  or or_7 (or_7_out, RAM_DOOR_MINI, RAM_DOOR);
  DisplayHelper displayhelper_1 (
    .mostleftbit(d_ff_49_q), .in_2(d_ff_50_q), .in_3(d_ff_51_q), .mostrightbit(d_ff_52_q), .Clk(Clk),
    .mid0(displayhelper_1_mid0), .topleft0(displayhelper_1_topleft0), .top0(displayhelper_1_top0),
    .topright0(displayhelper_1_topright0), .botright0(displayhelper_1_botright0),
    .bot0(displayhelper_1_bot0), .botleft0(displayhelper_1_botleft0), .bit1_0(displayhelper_1_bit1_0),
    .bit1_1(displayhelper_1_bit1_1));
  _7_Segment_Display u_7_segment_display_1 (
    .b(displayhelper_1_bit1_1), .c(displayhelper_1_bit1_0));  // open: g, f, a, e, d, dp
  _7_Segment_Display u_7_segment_display_2 (
    .g(displayhelper_1_mid0), .f(displayhelper_1_topleft0), .a(displayhelper_1_top0),
    .b(displayhelper_1_topright0), .e(displayhelper_1_botleft0), .d(displayhelper_1_bot0),
    .c(displayhelper_1_botright0));  // open: dp
  or or_8 (or_8_out, and_85_out, or_12_out);
  or or_9 (or_9_out, and_76_out, or_13_out);
  or or_10 (or_10_out, and_75_out, or_14_out);
  or or_11 (or_11_out, and_74_out, or_15_out);
  or or_12 (or_12_out, and_94_out, or_23_out);
  and and_94 (and_94_out, REGISTER_DOOR, d_ff_31_q);
  and and_95 (and_95_out, REGISTER_DOOR, d_ff_30_q);
  or or_13 (or_13_out, and_95_out, or_21_out);
  or or_14 (or_14_out, and_96_out, or_22_out);
  and and_96 (and_96_out, REGISTER_DOOR, d_ff_29_q);
  or or_15 (or_15_out, and_97_out, or_20_out);
  and and_97 (and_97_out, REGISTER_DOOR, d_ff_28_q);
  or or_16 (or_16_out, REGISTER_DOOR, WRITE_RESULT);
  and and_98 (and_98_out, or_8_out, or_16_out);
  and and_99 (and_99_out, or_9_out, or_16_out);
  and and_100 (and_100_out, or_10_out, or_16_out);
  and and_101 (and_101_out, or_11_out, or_16_out);
  and and_102 (and_102_out, or_8_out, REGISTER_DOOR);
  and and_103 (and_103_out, or_9_out, REGISTER_DOOR);
  and and_104 (and_104_out, or_10_out, REGISTER_DOOR);
  and and_105 (and_105_out, or_11_out, REGISTER_DOOR);
  Clock clock_4 (.out(Clk));
  or or_17 (or_17_out, not_15_out, WRITE_RESULT);
  not not_15 (not_15_out, REGIST);
  not not_16 (not_16_out, REGIST);
  and and_106 (and_106_out, and_98_out, or_17_out);
  and and_107 (and_107_out, and_99_out, or_17_out);
  and and_108 (and_108_out, and_100_out, or_17_out);
  and and_109 (and_109_out, and_101_out, or_17_out);
  and and_110 (and_110_out, and_102_out, REGIST);
  and and_111 (and_111_out, and_103_out, REGIST);
  and and_112 (and_112_out, and_104_out, REGIST);
  and and_113 (and_113_out, and_105_out, REGIST);
  not not_17 (not_17_out, REGIST);
  and and_114 (and_114_out, not_16_out, and_115_out);
  and and_115 (and_115_out, REGIST_SAVE, Clk);
  and and_116 (and_116_out, Clk, R1_Read_Write_out);
  and and_117 (and_117_out, not_17_out, A6_RIGHT_DOOR);
  or or_18 (or_18_out, A6_LEFT_DOOR, and_114_out, and_117_out);
  D_Flip_Flop d_ff_53 (.D(and_110_out), .clk(and_116_out), .Q(d_ff_53_q));  // open: Qn, preset, reset
  D_Flip_Flop d_ff_54 (.D(and_111_out), .clk(and_116_out), .Q(d_ff_54_q));  // open: Qn, preset, reset
  D_Flip_Flop d_ff_55 (.D(and_112_out), .clk(and_116_out), .Q(d_ff_55_q));  // open: Qn, preset, reset
  D_Flip_Flop d_ff_56 (.D(and_113_out), .clk(and_116_out), .Q(d_ff_56_q));  // open: Qn, preset, reset
  and and_118 (and_118_out, REGIST, and_119_out);
  and and_119 (and_119_out, REGIST_SAVE, Clk);
  and and_120 (and_120_out, A6_RIGHT_DOOR, REGIST);
  and and_121 (and_121_out, gotoIR, Clk);
  or R0_Read_Write (R0_Read_Write_out, WRITE_RESULT, and_127_out);
  and and_122 (and_122_out, Clk, R0_Read_Write_out);
  or or_19 (or_19_out, and_120_out, and_118_out);
  and R1_Read_Write (R1_Read_Write_out, REGISTER_DOOR, REGIST);
  and and_123 (and_123_out, or_19_out, d_ff_53_q);
  and and_124 (and_124_out, or_19_out, d_ff_54_q);
  and and_125 (and_125_out, or_19_out, d_ff_55_q);
  and and_126 (and_126_out, or_19_out, d_ff_56_q);
  or or_20 (or_20_out, and_126_out, or_24_out);
  and and_127 (and_127_out, REGISTER_DOOR, not_18_out);
  D_Flip_Flop d_ff_57 (.D(and_106_out), .clk(and_122_out), .Q(d_ff_57_q));  // open: Qn, preset, reset
  D_Flip_Flop d_ff_58 (.D(and_107_out), .clk(and_122_out), .Q(d_ff_58_q));  // open: Qn, preset, reset
  D_Flip_Flop d_ff_59 (.D(and_108_out), .clk(and_122_out), .Q(d_ff_59_q));  // open: Qn, preset, reset
  D_Flip_Flop d_ff_60 (.D(and_109_out), .clk(and_122_out), .Q(d_ff_60_q));  // open: Qn, preset, reset
  or or_21 (or_21_out, and_124_out, or_25_out);
  or or_22 (or_22_out, and_125_out, or_26_out);
  D_Flip_Flop d_ff_61 (.D(d_ff_28_q), .clk(and_121_out), .Q(d_ff_61_q));  // open: Qn, preset, reset
  D_Flip_Flop d_ff_62 (.D(d_ff_29_q), .clk(and_121_out), .Q(d_ff_62_q));  // open: Qn, preset, reset
  D_Flip_Flop d_ff_63 (.D(d_ff_30_q), .clk(and_121_out), .Q(d_ff_63_q));  // open: Qn, preset, reset
  D_Flip_Flop d_ff_64 (.D(d_ff_31_q), .clk(and_121_out), .Q(d_ff_64_q));  // open: Qn, preset, reset
  not not_18 (not_18_out, REGIST);
  and and_128 (and_128_out, or_18_out, d_ff_57_q);
  and and_129 (and_129_out, or_18_out, d_ff_58_q);
  and and_130 (and_130_out, or_18_out, d_ff_59_q);
  and and_131 (and_131_out, or_18_out, d_ff_60_q);
  or or_23 (or_23_out, and_123_out, or_27_out);
  or or_24 (or_24_out, and_131_out, or_29_out);
  or or_25 (or_25_out, and_129_out, or_31_out);
  or or_26 (or_26_out, and_130_out, or_28_out);
  or or_27 (or_27_out, and_128_out, or_30_out);
  Clock clock_5 (.out(Clk));
  and and_132 (and_132_out, Clk, A6_LEFT_DOOR);
  and and_133 (and_133_out, Clk, A6_RIGHT_DOOR);
  D_Flip_Flop d_ff_65 (.D(or_11_out), .clk(and_132_out), .Q(d_ff_65_q));  // open: Qn, preset, reset
  D_Flip_Flop d_ff_66 (.D(or_10_out), .clk(and_132_out), .Q(d_ff_66_q));  // open: Qn, preset, reset
  D_Flip_Flop d_ff_67 (.D(or_9_out), .clk(and_132_out), .Q(d_ff_67_q));  // open: Qn, preset, reset
  D_Flip_Flop d_ff_68 (.D(or_8_out), .clk(and_132_out), .Q(d_ff_68_q));  // open: Qn, preset, reset
  D_Flip_Flop d_ff_69 (.D(or_11_out), .clk(and_133_out), .Q(d_ff_69_q));  // open: Qn, preset, reset
  D_Flip_Flop d_ff_70 (.D(or_10_out), .clk(and_133_out), .Q(d_ff_70_q));  // open: Qn, preset, reset
  D_Flip_Flop d_ff_71 (.D(or_9_out), .clk(and_133_out), .Q(d_ff_71_q));  // open: Qn, preset, reset
  D_Flip_Flop d_ff_72 (.D(or_8_out), .clk(and_133_out), .Q(d_ff_72_q));  // open: Qn, preset, reset
  or or_28 (or_28_out, and_142_out, in_6);
  or or_29 (or_29_out, and_146_out, in_7);
  and and_134 (and_134_out, gotoCU, Clk);
  and and_135 (and_135_out, COMPUTE, Clk);
  or or_30 (or_30_out, and_136_out, in_4);
  or or_31 (or_31_out, and_141_out, in_5);
  A6 a6_1 (
    .L_input(d_ff_65_q), .in_2(d_ff_66_q), .in_3(d_ff_67_q), .in_4(d_ff_68_q), .R_input(d_ff_69_q),
    .in_6(d_ff_70_q), .in_7(d_ff_71_q), .in_8(d_ff_72_q), .Clk(COMPUTE), .add0_sub1(SUB),
    .SignedOverflow(SIGNED_OVERLOAD), .Zero(ZERO), .Negative(NEGATIVE), .Overflow(OVERFLOW),
    .out_15(a6_1_out_15), .out_16(a6_1_out_16), .out_17(a6_1_out_17), .out_18(a6_1_out_18));
  D_Flip_Flop d_ff_73 (.D(a6_1_out_18), .clk(and_135_out), .Q(d_ff_73_q));  // open: Qn, preset, reset
  D_Flip_Flop d_ff_74 (.D(a6_1_out_16), .clk(and_135_out), .Q(d_ff_74_q));  // open: Qn, preset, reset
  D_Flip_Flop d_ff_75 (.D(a6_1_out_17), .clk(and_135_out), .Q(d_ff_75_q));  // open: Qn, preset, reset
  D_Flip_Flop d_ff_76 (.D(d_ff_61_q), .clk(and_134_out), .Q(d_ff_76_q));  // open: Qn, preset, reset
  D_Flip_Flop d_ff_77 (.D(d_ff_62_q), .clk(and_134_out), .Q(d_ff_77_q));  // open: Qn, preset, reset
  D_Flip_Flop d_ff_78 (.D(d_ff_63_q), .clk(and_134_out), .Q(d_ff_78_q));  // open: Qn, preset, reset
  D_Flip_Flop d_ff_79 (.D(d_ff_64_q), .clk(and_134_out), .Q(d_ff_79_q));  // open: Qn, preset, reset
  D_Flip_Flop d_ff_80 (.D(a6_1_out_15), .clk(and_135_out), .Q(d_ff_80_q));  // open: Qn, preset, reset
  not not_19 (not_19_out, HALT);
  or or_32 (or_32_out, ADD, SUB);
  and and_136 (and_136_out, WRITE_RESULT, d_ff_73_q);
  and and_137 (and_137_out, d_ff_76_q, not_19_out, or_33_out);
  and and_138 (and_138_out, d_ff_77_q, not_19_out, or_33_out);
  and and_139 (REGIST, d_ff_78_q, not_19_out, or_33_out);
  and and_140 (RAM_MINI_INSTRUCTION, d_ff_79_q, not_19_out, or_33_out);
  or or_33 (or_33_out, MINI_INSTRUCTION_START, or_35_out, or_36_out, REGIST_SAVE);
  and and_141 (and_141_out, WRITE_RESULT, d_ff_75_q);
  and and_142 (and_142_out, WRITE_RESULT, d_ff_74_q);
  and and_143 (and_143_out, MINI_INSTRUCTION_START, LOAD);
  and and_144 (and_144_out, MINI_INSTRUCTION_START, SAVE);
  and and_145 (A6_LEFT_DOOR, MINI_INSTRUCTION_START, or_32_out);
  and and_146 (and_146_out, WRITE_RESULT, d_ff_80_q);
  D_Flip_Flop d_ff_81 (.D(and_143_out), .clk(Clk), .Q(d_ff_81_q));  // open: Qn, preset, reset
  D_Flip_Flop d_ff_82 (.D(A6_LEFT_DOOR), .clk(Clk), .Q(A6_RIGHT_DOOR));  // open: Qn, preset, reset
  Clock clock_6 (.out(Clk));
  and and_147 (HALT, REGIST, RAM_MINI_INSTRUCTION, and_138_out, and_137_out);
  D_Flip_Flop d_ff_83 (.D(and_144_out), .clk(Clk), .Q(REGIST_SAVE));  // open: Qn, preset, reset
  not not_20 (LOAD, or_34_out);
  or or_34 (or_34_out, and_138_out, and_137_out);
  or or_35 (or_35_out, d_ff_81_q, RAM_DOOR_MINI, REGISTER_DOOR);
  or or_36 (or_36_out, A6_RIGHT_DOOR, WRITE_RESULT, COMPUTE);
  or or_37 (MINI_INSTRUCTION_COMPUTE, or_35_out, or_36_out, REGIST_SAVE);
  and and_148 (SAVE, not_21_out, and_138_out);
  not not_21 (not_21_out, and_137_out);
  D_Flip_Flop d_ff_84 (.D(d_ff_81_q), .clk(Clk), .Q(RAM_DOOR_MINI));  // open: Qn, preset, reset
  Clock clock_7 (.out(Clk));
  and and_149 (ADD, and_137_out, not_22_out);
  not not_22 (not_22_out, and_138_out);
  D_Flip_Flop d_ff_85 (.D(RAM_DOOR_MINI), .clk(Clk), .Q(REGISTER_DOOR));  // open: Qn, preset, reset
  D_Flip_Flop d_ff_86 (.D(A6_RIGHT_DOOR), .clk(Clk), .Q(COMPUTE));  // open: Qn, preset, reset
  PC pc_1 (
    .HaltIn(HALT), .CUsignal(MINI_INSTRUCTION_END), .inputBit_2(in_1), .inputBit_1(in_2), .inputBit_0(in_3),
    .Clk(Clk), .HaltOut(pc_1_haltout), .outBit2(pc_1_outbit2), .outBit1(pc_1_outbit1), .outBit0(pc_1_outbit0));
  and and_150 (SUB, and_137_out, and_138_out, not_23_out);
  not not_23 (not_23_out, RAM_MINI_INSTRUCTION);
  D_Flip_Flop d_ff_87 (.D(1'b1), .clk(Clk), .Q(d_ff_87_q));  // open: Qn, preset, reset
  buf or_38 (or_38_out, in_11);  // OR_Gate
  D_Flip_Flop d_ff_88 (.D(REGIST_SAVE), .clk(Clk), .Q(d_ff_88_q));  // open: Qn, preset, reset
  D_Flip_Flop d_ff_89 (.D(COMPUTE), .clk(Clk), .Q(WRITE_RESULT));  // open: Qn, preset, reset
  and and_151 (and_151_out, d_ff_87_q, not_24_out, pc_1_haltout);
  not not_24 (not_24_out, or_40_out);
  and and_152 (and_152_out, pc_1_outbit2, or_39_out);
  and and_153 (and_153_out, pc_1_outbit1, or_39_out);
  and and_154 (and_154_out, pc_1_outbit0, or_39_out);
  D_Flip_Flop d_ff_90 (.D(REGISTER_DOOR), .clk(Clk), .Q(d_ff_90_q));  // open: Qn, preset, reset
  D_Flip_Flop d_ff_91 (.D(WRITE_RESULT), .clk(Clk), .Q(d_ff_91_q));  // open: Qn, preset, reset
  or or_39 (or_39_out, d_ff_92_q, and_151_out);
  or or_40 (or_40_out, d_ff_92_q, d_ff_93_q, RAM_DOOR, gotoIR, gotoCU, MINI_INSTRUCTION_START, MINI_INSTRUCTION_COMPUTE);
  D_Flip_Flop d_ff_92 (.D(and_151_out), .clk(Clk), .Q(d_ff_92_q));  // open: Qn, preset, reset
  and and_155 (and_155_out, 1'b1, RAM_MINI_INSTRUCTION);
  D_Flip_Flop d_ff_93 (.D(d_ff_92_q), .clk(Clk), .Q(d_ff_93_q));  // open: Qn, preset, reset
  or or_41 (or_41_out, and_152_out, 1'b0);
  or or_42 (or_42_out, and_153_out, 1'b0);
  or or_43 (or_43_out, and_154_out, and_155_out);
  D_Flip_Flop d_ff_94 (.D(d_ff_93_q), .clk(Clk), .Q(RAM_DOOR));  // open: Qn, preset, reset
  D_Flip_Flop d_ff_95 (.D(RAM_DOOR), .clk(Clk), .Q(gotoIR));  // open: Qn, preset, reset
  D_Flip_Flop d_ff_96 (.D(or_41_out), .clk(Clk), .Q(d_ff_96_q));  // open: Qn, preset, reset
  D_Flip_Flop d_ff_97 (.D(or_42_out), .clk(Clk), .Q(d_ff_97_q));  // open: Qn, preset, reset
  D_Flip_Flop d_ff_98 (.D(or_43_out), .clk(Clk), .Q(d_ff_98_q));  // open: Qn, preset, reset
  or or_44 (MINI_INSTRUCTION_END, d_ff_90_q, d_ff_88_q, d_ff_91_q);
  D_Flip_Flop d_ff_99 (.D(gotoIR), .clk(Clk), .Q(gotoCU));  // open: Qn, preset, reset
  D_Flip_Flop d_ff_100 (.D(gotoCU), .clk(Clk), .Q(MINI_INSTRUCTION_START));  // open: Qn, preset, reset
  or or_45 (or_45_out, d_ff_96_q, in_10);
  or or_46 (or_46_out, d_ff_97_q, in_9);
  or or_47 (or_47_out, d_ff_98_q, in_8);

  // Other names for the same wires on the sheet: R0_OUT = A6_LEFT_DOOR; REGIST_OUT = A6_RIGHT_DOOR;
  //   SAVE_DOOR = REGIST_SAVE; SEND_TO_BUS = REGISTER_DOOR; WRITE = REGISTER_DOOR

  // Notes on the sheet:
  //   A5
  //   TURN MODE REGISTER ON BEFORE START
  //   MBR
  //   4-bit data output pins
  //   0=read
  //   1=write
  //   IR
  //   R1
  //   R0
  //   Control Unit
  //   PC
  //   Fetch cycle
  //   to extend to ram to 0 or 1
  //   when doing load or save
  //   MAR
  //   U-Bus
  //   4-bit data
  //   3-bit address
  //   1-bit mode
endmodule

module A6 (
  input  L_input,
  input  in_2,
  input  in_3,
  input  in_4,
  input  R_input,
  input  in_6,
  input  in_7,
  input  in_8,
  input  Clk,
  input  add0_sub1,
  output SignedOverflow,
  output Zero,
  output Negative,
  output Overflow,
  output out_15,
  output out_16,
  output out_17,
  output out_18
);

  wire and_1_out, and_2_out, and_3_out, and_4_out, and_5_out, and_6_out, and_7_out, and_8_out, and_9_out,
       and_10_out, and_11_out, and_12_out, and_13_out, and_14_out, and_15_out, and_16_out, and_17_out,
       and_18_out, and_19_out, and_20_out, and_21_out, and_22_out, and_24_out, and_26_out, and_27_out,
       filleradder_1_c, filleradder_2_c, filleradder_3_c, Neg_out, not_1_out, not_2_out, not_3_out,
       not_4_out, not_5_out, not_6_out, not_7_out, not_8_out, not_9_out, not_10_out, not_11_out, not_12_out,
       not_13_out, not_14_out, not_15_out, or_1_out, or_2_out, or_3_out, or_4_out, or_5_out, Pos_out,
       xor_2_out, xor_3_out, xor_4_out, xor_5_out;

  not not_1 (not_1_out, add0_sub1);
  and and_1 (and_1_out, L_input, Clk);
  and and_2 (and_2_out, in_2, Clk);
  and and_3 (and_3_out, in_3, Clk);
  FillerAdder filleradder_1 (.A(or_1_out), .B(and_1_out), .Carry(filleradder_2_c), .C(filleradder_1_c), .Sum(Negative));
  and and_4 (and_4_out, in_4, Clk);
  FillerAdder filleradder_2 (.A(or_2_out), .B(and_2_out), .Carry(filleradder_3_c), .C(filleradder_2_c), .Sum(out_16));
  or or_1 (or_1_out, xor_2_out, and_6_out);
  FillerAdder filleradder_3 (.A(or_3_out), .B(and_3_out), .Carry(and_5_out), .C(filleradder_3_c), .Sum(out_17));
  or or_2 (or_2_out, xor_3_out, and_8_out);
  or or_3 (or_3_out, xor_4_out, and_9_out);
  and and_5 (and_5_out, and_4_out, or_4_out);
  xor xor_1 (out_18, and_4_out, or_4_out);
  and and_6 (and_6_out, and_12_out, not_1_out);
  and and_7 (and_7_out, not_6_out, and_10_out);
  or or_4 (or_4_out, xor_5_out, and_14_out);
  not not_2 (not_2_out, out_18);
  not not_3 (not_3_out, out_17);
  not not_4 (not_4_out, out_16);
  not not_5 (not_5_out, Negative);
  and and_8 (and_8_out, and_13_out, not_1_out);
  and and_9 (and_9_out, and_17_out, not_1_out);
  xor xor_2 (xor_2_out, not_6_out, and_10_out);
  and and_10 (and_10_out, not_10_out, and_16_out);
  and and_11 (and_11_out, not_2_out, not_3_out, not_4_out, not_5_out);
  and and_12 (and_12_out, R_input, Clk);
  and and_13 (and_13_out, in_6, Clk);
  and and_14 (and_14_out, and_18_out, not_1_out);
  and and_15 (and_15_out, and_12_out, add0_sub1);
  not not_6 (not_6_out, and_15_out);
  xor xor_3 (xor_3_out, not_10_out, and_16_out);
  and and_16 (and_16_out, not_11_out, and_22_out);
  not not_7 (not_7_out, or_1_out);
  not not_8 (not_8_out, and_1_out);
  not not_9 (not_9_out, or_1_out);
  and and_17 (and_17_out, in_7, Clk);
  and and_18 (and_18_out, in_8, Clk);
  and and_19 (and_19_out, and_13_out, add0_sub1);
  and and_20 (and_20_out, and_17_out, add0_sub1);
  and and_21 (and_21_out, and_18_out, add0_sub1);
  not not_10 (not_10_out, and_19_out);
  not not_11 (not_11_out, and_20_out);
  not not_12 (not_12_out, and_21_out);
  xor xor_4 (xor_4_out, not_11_out, and_22_out);
  and and_22 (and_22_out, not_12_out, 1'b1);
  and Neg (Neg_out, or_1_out, and_1_out);
  and Pos (Pos_out, not_7_out, not_8_out);
  and and_23 (Zero, and_11_out, Clk);
  xor xor_5 (xor_5_out, not_12_out, 1'b1);
  and and_24 (and_24_out, Negative, Neg_out);
  and and_25 (SignedOverflow, Pos_out, Negative);
  and and_26 (and_26_out, not_13_out, not_9_out, filleradder_1_c);
  not not_13 (not_13_out, add0_sub1);
  not not_14 (not_14_out, filleradder_1_c);
  and and_27 (and_27_out, and_24_out, not_14_out);
  or or_5 (or_5_out, and_26_out, and_27_out);
  not not_15 (not_15_out, Zero);
  and notZero (Overflow, or_5_out, not_15_out);

  assign out_15 = Negative;

  // Other names for the same wires on the sheet: CMD = add0_sub1

  // Notes on the sheet:
  //   0 add, 1 sub
  //   Add/Sub command
  //   B Input
  //   L input
  //   A-out output
  //   A Input
  //   Adder
  //   R Input
  //   2's Complement
  //   Status output
  //   -8 + -8 is underflow (not supported)
endmodule

module FillerAdder (
  input  A,
  input  B,
  input  Carry,
  output C,
  output Sum
);

  wire and_1_out, and_2_out, xor_1_out;

  and and_1 (and_1_out, A, B);
  xor xor_1 (xor_1_out, A, B);
  and and_2 (and_2_out, xor_1_out, Carry);
  or or_1 (C, and_1_out, and_2_out);
  xor xor_2 (Sum, xor_1_out, Carry);
endmodule

module DisplayHelper (
  input  mostleftbit,
  input  in_2,
  input  in_3,
  input  mostrightbit,
  input  Clk,
  output mid0,
  output topleft0,
  output top0,
  output topright0,
  output botright0,
  output bot0,
  output botleft0,
  output bit1_0,
  output bit1_1
);

  wire and_1_out, and_2_out, and_4_out, and_5_out, and_6_out, and_8_out, and_9_out, and_11_out, and_12_out,
       and_13_out, and_14_out, and_16_out, and_18_out, and_19_out, and_21_out, and_22_out, and_23_out,
       and_24_out, and_26_out, and_27_out, and_29_out, and_30_out, and_31_out, and_32_out, and_33_out,
       Bot_out, BotLeft_out, BotRight_out, Mid_out, not_1_out, not_2_out, not_3_out, not_4_out, not_5_out,
       not_6_out, not_7_out, not_8_out, not_9_out, not_10_out, not_11_out, not_12_out, not_13_out,
       not_14_out, not_15_out, or_1_out, or_2_out, or_3_out, or_4_out, or_5_out, or_6_out, or_7_out,
       or_8_out, or_9_out, or_10_out, or_11_out, or_12_out, or_13_out, or_14_out, or_15_out, or_16_out,
       or_17_out, or_18_out, Top_out, TopLeft_out, TopRight_out;

  or or_1 (or_1_out, mostrightbit, in_3, in_2, mostleftbit);
  not not_1 (not_1_out, or_1_out);
  or or_2 (or_2_out, in_3, in_2, mostleftbit);
  not not_2 (not_2_out, or_2_out);
  or or_3 (or_3_out, not_1_out, and_22_out);
  and and_1 (and_1_out, not_2_out, mostrightbit);
  or or_4 (or_4_out, and_1_out, and_24_out);
  or or_5 (or_5_out, mostleftbit, in_2, mostrightbit);
  not not_3 (not_3_out, or_5_out);
  and and_2 (and_2_out, not_3_out, in_3);
  or or_6 (or_6_out, and_2_out, and_26_out);
  or Mid (Mid_out, or_6_out, or_8_out, or_10_out, or_12_out, and_12_out, and_16_out, and_19_out);
  and and_3 (mid0, Clk, Mid_out);
  or or_7 (or_7_out, in_2, mostleftbit);
  and and_4 (and_4_out, mostrightbit, in_3);
  not not_4 (not_4_out, or_7_out);
  and and_5 (and_5_out, not_4_out, and_4_out);
  or or_8 (or_8_out, and_5_out, and_30_out);
  or or_9 (or_9_out, mostleftbit, in_3, mostrightbit);
  not not_5 (not_5_out, or_9_out);
  and and_6 (and_6_out, not_5_out, in_2);
  or or_10 (or_10_out, and_6_out, and_32_out);
  or TopLeft (TopLeft_out, or_3_out, or_10_out, or_12_out, and_12_out, and_16_out, and_19_out);
  and and_7 (topleft0, Clk, TopLeft_out);
  or or_11 (or_11_out, mostleftbit, in_3);
  not not_6 (not_6_out, or_11_out);
  and and_8 (and_8_out, in_2, mostrightbit);
  and and_9 (and_9_out, not_6_out, and_8_out);
  or or_12 (or_12_out, and_9_out, and_33_out);
  or Top (Top_out, or_3_out, or_6_out, or_8_out, or_12_out, and_12_out, and_14_out, and_16_out, and_19_out);
  and and_10 (top0, Clk, Top_out);
  or or_13 (or_13_out, mostleftbit, mostrightbit);
  and and_11 (and_11_out, in_3, in_2);
  not not_7 (not_7_out, or_13_out);
  and and_12 (and_12_out, not_7_out, and_11_out);
  and and_13 (and_13_out, mostrightbit, in_2, in_3);
  not not_8 (not_8_out, mostleftbit);
  and and_14 (and_14_out, not_8_out, and_13_out);
  or TopRight (TopRight_out, or_3_out, or_4_out, or_6_out, or_8_out, or_10_out, and_14_out, and_16_out, and_19_out);
  and and_15 (topright0, Clk, TopRight_out);
  or or_14 (or_14_out, mostrightbit, in_3, in_2);
  not not_9 (not_9_out, or_14_out);
  and and_16 (and_16_out, not_9_out, mostleftbit);
  and and_17 (botright0, Clk, BotRight_out);
  or or_15 (or_15_out, in_3, in_2);
  not not_10 (not_10_out, or_15_out);
  or BotRight (BotRight_out, or_3_out, or_4_out, or_8_out, or_10_out, or_12_out, and_12_out, and_14_out, and_16_out, and_19_out);
  and and_18 (and_18_out, mostrightbit, mostleftbit);
  and and_19 (and_19_out, not_10_out, and_18_out);
  or Bot (Bot_out, or_3_out, or_6_out, or_8_out, or_12_out, and_12_out, and_16_out);
  and and_20 (bot0, Clk, Bot_out);
  or or_16 (or_16_out, in_2, mostrightbit);
  and and_21 (and_21_out, in_3, mostleftbit);
  not not_11 (not_11_out, or_16_out);
  and and_22 (and_22_out, not_11_out, and_21_out);
  and and_23 (and_23_out, in_3, mostrightbit, mostleftbit);
  not not_12 (not_12_out, in_2);
  and and_24 (and_24_out, not_12_out, and_23_out);
  or BotLeft (BotLeft_out, or_3_out, or_6_out, and_12_out, and_16_out);
  and and_25 (botleft0, Clk, BotLeft_out);
  or or_17 (or_17_out, mostrightbit, in_3);
  not not_13 (not_13_out, or_17_out);
  and and_26 (and_26_out, not_13_out, and_27_out);
  and and_27 (and_27_out, mostleftbit, in_2);
  not not_14 (not_14_out, in_3);
  or or_18 (or_18_out, and_22_out, and_24_out, and_26_out, and_30_out, and_32_out, and_33_out);
  and and_28 (bit1_0, Clk, or_18_out);
  and and_29 (and_29_out, mostrightbit, in_2, mostleftbit);
  and and_30 (and_30_out, not_14_out, and_29_out);
  and and_31 (and_31_out, in_3, in_2, mostleftbit);
  not not_15 (not_15_out, mostrightbit);
  and and_32 (and_32_out, not_15_out, and_31_out);
  and and_33 (and_33_out, mostrightbit, in_3, in_2, mostleftbit);

  assign bit1_1 = bit1_0;

  // Notes on the sheet:
  //   Created a circuit to help display
  //   names for wires are personal notes
  //   0000
  //   0001
  //   0010
  //   0011
  //   0100
  //   0101
  //   0110
  //   0111
  //   1000
  //   1001
  //   1010
  //   1011
  //   1100
  //   1101
  //   1110
  //   1111
endmodule

module PC (
  input  HaltIn,
  input  CUsignal,
  input  inputBit_2,
  input  inputBit_1,
  input  inputBit_0,
  input  Clk,
  output HaltOut,
  output outBit2,
  output outBit1,
  output outBit0
);

  wire and_1_out, and_2_out, and_3_out, and_4_out, and_5_out, and_6_out, and_7_out, d_ff_1_q, not_1_out,
       or_1_out, or_2_out, or_3_out, xor_1_out, xor_2_out, xor_3_out;

  not not_1 (not_1_out, and_5_out);
  and and_1 (and_1_out, not_1_out, inputBit_2);
  and and_2 (and_2_out, not_1_out, inputBit_1);
  and and_3 (and_3_out, not_1_out, inputBit_0);
  and and_4 (and_4_out, 1'b1, and_5_out, CUsignal);
  and and_5 (and_5_out, d_ff_1_q, HaltOut);
  and and_6 (and_6_out, and_4_out, outBit0);
  xor xor_1 (xor_1_out, and_4_out, outBit0);
  D_Flip_Flop d_ff_1 (.D(1'b1), .clk(CUsignal), .Q(d_ff_1_q));  // open: Qn, preset, reset
  and and_7 (and_7_out, and_6_out, outBit1);
  xor xor_2 (xor_2_out, and_6_out, outBit1);
  or or_1 (or_1_out, and_3_out, xor_1_out);
  or or_2 (or_2_out, xor_2_out, and_2_out);
  not not_2 (HaltOut, HaltIn);
  xor xor_3 (xor_3_out, and_7_out, outBit2);
  or or_3 (or_3_out, xor_3_out, and_1_out);
  D_Flip_Flop d_ff_2 (.D(or_3_out), .clk(Clk), .Q(outBit2));  // open: Qn, preset, reset
  D_Flip_Flop d_ff_3 (.D(or_2_out), .clk(Clk), .Q(outBit1));  // open: Qn, preset, reset
  D_Flip_Flop d_ff_4 (.D(or_1_out), .clk(Clk), .Q(outBit0));  // open: Qn, preset, reset

  // Notes on the sheet:
  //   signals to tell you that you finished instruction
  //   on to start next cycle
endmodule
